# Fritzing sketch Fritzing (saved by Fritzing 0.9.3b)

parts:
  Motor_Driver = Motor Driver 1A Dual TB6612FNG
  M1 = DC Motor
  M2 = DC Motor
  Battery = 4 x AAA Battery Mount
  Raspberry_Pi_3 = Raspberry Pi 3 [part_number=RPI-3-V1.2]

nets:
  N1: Motor_Driver.B01, M2.pin_1
  N2: Motor_Driver.B02, M2.pin_2
  N3: Motor_Driver.A02, M1.pin_1
  N4: Motor_Driver.A01, M1.pin_2
  GND: Motor_Driver.GND, Battery.+, Raspberry_Pi_3.GND
  3V3: Motor_Driver.VCC, Raspberry_Pi_3.3v3, Raspberry_Pi_3.3V3
  N5: Motor_Driver.VM, Battery.-
  N6: Motor_Driver.PWMA, Raspberry_Pi_3.GPIO4
  N7: Motor_Driver.AIN2, Raspberry_Pi_3.GPIO5
  N8: Motor_Driver.AIN1, Raspberry_Pi_3.GPIO6
  N9: Motor_Driver.STBY, Raspberry_Pi_3.GPIO10
  N10: Motor_Driver.BIN1, Raspberry_Pi_3.GPIO8
  N11: Motor_Driver.BIN2, Raspberry_Pi_3.GPIO9
  N12: Motor_Driver.PWMB, Raspberry_Pi_3.GPIO7
